// Logisim project videoadapterebat.circ as structural Verilog: 6 circuits, main circuit main
module main (
  input  reset,
  input  change_value,
  input  [3:0] column,
  input  _0_if_start_pos_else_1,
  input  [3:0] row,
  output [15:0] out_6,
  output [15:0] out_7,
  output [15:0] out_8,
  output [15:0] out_9,
  output [15:0] out_10,
  output [15:0] out_11,
  output [15:0] out_12,
  output [15:0] out_13,
  output [15:0] out_14,
  output [15:0] out_15,
  output [15:0] out_16,
  output [15:0] out_17,
  output [15:0] out_18,
  output [15:0] out_19,
  output [15:0] out_20,
  output [15:0] out_21
);

  wire decoder_1_out0, decoder_1_out1, decoder_1_out2, decoder_1_out3, decoder_1_out4, decoder_1_out5,
       decoder_1_out6, decoder_1_out7, decoder_1_out8, decoder_1_out9, decoder_1_out10, decoder_1_out11,
       decoder_1_out12, decoder_1_out13, decoder_1_out14, decoder_1_out15, or_1_out;

  Decoder #(.select(4)) decoder_1 (
    .out0(decoder_1_out0), .out1(decoder_1_out1), .out2(decoder_1_out2), .out3(decoder_1_out3),
    .out4(decoder_1_out4), .out5(decoder_1_out5), .out6(decoder_1_out6), .out7(decoder_1_out7),
    .out8(decoder_1_out8), .out9(decoder_1_out9), .out10(decoder_1_out10), .out11(decoder_1_out11),
    .out12(decoder_1_out12), .out13(decoder_1_out13), .out14(decoder_1_out14), .out15(decoder_1_out15),
    .sel(column));  // open: en
  or or_1 (or_1_out, reset, _0_if_start_pos_else_1);
  videoadapterRowcontrol videoadapterrowcontrol_1 (
    .id(decoder_1_out0), .rownumb(row), .save(change_value), .reset(or_1_out), .outputValue(out_6));
  videoadapterRowcontrol videoadapterrowcontrol_2 (
    .id(decoder_1_out1), .rownumb(row), .save(change_value), .reset(or_1_out), .outputValue(out_7));
  videoadapterRowcontrol videoadapterrowcontrol_3 (
    .id(decoder_1_out2), .rownumb(row), .save(change_value), .reset(or_1_out), .outputValue(out_8));
  videoadapterRowcontrol videoadapterrowcontrol_4 (
    .id(decoder_1_out3), .rownumb(row), .save(change_value), .reset(or_1_out), .outputValue(out_9));
  videoadapterRowcontrol videoadapterrowcontrol_5 (
    .id(decoder_1_out4), .rownumb(row), .save(change_value), .reset(or_1_out), .outputValue(out_10));
  videoadapterRowcontrol videoadapterrowcontrol_6 (
    .id(decoder_1_out5), .rownumb(row), .save(change_value), .reset(or_1_out), .outputValue(out_11));
  videoadapterRowcontrol videoadapterrowcontrol_7 (
    .id(decoder_1_out6), .rownumb(row), .save(change_value), .reset(or_1_out), .outputValue(out_12));
  videoadapterRowcontrol videoadapterrowcontrol_8 (
    .id(decoder_1_out7), .rownumb(row), .save(change_value), .reset(or_1_out), .outputValue(out_13));
  videoadapterRowcontrol videoadapterrowcontrol_9 (
    .id(decoder_1_out8), .rownumb(row), .save(change_value), .reset(or_1_out), .outputValue(out_14));
  videoadapterRowcontrol videoadapterrowcontrol_10 (
    .id(decoder_1_out9), .rownumb(row), .save(change_value), .reset(or_1_out), .outputValue(out_15));
  videoadapterRowcontrol videoadapterrowcontrol_11 (
    .id(decoder_1_out10), .rownumb(row), .save(change_value), .reset(or_1_out), .outputValue(out_16));
  videoadapterRowcontrol videoadapterrowcontrol_12 (
    .id(decoder_1_out11), .rownumb(row), .save(change_value), .reset(or_1_out), .outputValue(out_17));
  videoadapterRowcontrol videoadapterrowcontrol_13 (
    .id(decoder_1_out12), .rownumb(row), .save(change_value), .reset(or_1_out), .outputValue(out_18));
  videoadapterRowcontrol videoadapterrowcontrol_14 (
    .id(decoder_1_out13), .rownumb(row), .save(change_value), .reset(or_1_out), .outputValue(out_19));
  videoadapterRowcontrol videoadapterrowcontrol_15 (
    .id(decoder_1_out14), .rownumb(row), .save(change_value), .reset(or_1_out), .outputValue(out_20));
  videoadapterRowcontrol videoadapterrowcontrol_16 (
    .id(decoder_1_out15), .rownumb(row), .save(change_value), .reset(or_1_out), .outputValue(out_21));
endmodule

module videoadapterRowcontrol (
  input  id,
  input  [3:0] rownumb,
  input  save,
  input  reset,
  output [15:0] outputValue
);

  wire [15:0] decoder_1_out0, xor_1_out;

  Decoder #(.select(4), .disabled(0)) decoder_1 (
    .out0(decoder_1_out0[0]), .out1(decoder_1_out0[1]), .out2(decoder_1_out0[2]), .out3(decoder_1_out0[3]),
    .out4(decoder_1_out0[4]), .out5(decoder_1_out0[5]), .out6(decoder_1_out0[6]), .out7(decoder_1_out0[7]),
    .out8(decoder_1_out0[8]), .out9(decoder_1_out0[9]), .out10(decoder_1_out0[10]),
    .out11(decoder_1_out0[11]), .out12(decoder_1_out0[12]), .out13(decoder_1_out0[13]),
    .out14(decoder_1_out0[14]), .out15(decoder_1_out0[15]), .sel(rownumb));  // open: en
  assign xor_1_out = decoder_1_out0 ^ outputValue;  // XOR_Gate xor_1, 16 bits wide
  Register #(.width(16)) register_1 (.D(xor_1_out), .en(id), .Q(outputValue), .clk(save), .clr(reset));

  // Notes on the sheet:
  //   rownumb: pull=down
  //   save: pull=down
  //   reset: pull=down
  //   id: pull=down
endmodule

module test (
  input  [3:0] in_1,
  input  [3:0] in_2
);

  wire buffer_1_out, button_1_out, button_2_out, button_3_out, button_4_out, clock_1_out, comparator_1_eq,
       controlled_buffer_1_out, counter_1_q, or_1_out, reader_1_out_20;
  wire [7:0] ram_1_data, \reader_1_адрес_говна , \reader_1_значение_говна ;
  wire [15:0] main_1_out_6, main_1_out_7, main_1_out_8, main_1_out_9, main_1_out_10, main_1_out_11,
       main_1_out_12, main_1_out_13, main_1_out_14, main_1_out_15, main_1_out_16, main_1_out_17,
       main_1_out_18, main_1_out_19, main_1_out_20, main_1_out_21;

  Button button_1 (.out(button_1_out));
  or or_1 (or_1_out, comparator_1_eq, button_1_out);
  buf buffer_1 (buffer_1_out, or_1_out);
  Comparator #(.mode("unsigned")) comparator_1 (
    .a({8{1'b1}}), .b(\reader_1_адрес_говна ), .eq(comparator_1_eq));  // open: gt, lt
  Counter #(.width(1), .max('h1)) counter_1 (
    .D(buffer_1_out), .count(buffer_1_out), .Q(counter_1_q), .clk(buffer_1_out));  // open: load, carry, clr
  // Probe on in_2
  // Probe on in_1
  DotMatrix #(.matrixcols(16), .matrixrows(16)) dotmatrix_1 (
    .col0(main_1_out_6), .col1(main_1_out_7), .col2(main_1_out_8), .col3(main_1_out_9), .col4(main_1_out_10),
    .col5(main_1_out_11), .col6(main_1_out_12), .col7(main_1_out_13), .col8(main_1_out_14),
    .col9(main_1_out_15), .col10(main_1_out_16), .col11(main_1_out_17), .col12(main_1_out_18),
    .col13(main_1_out_19), .col14(main_1_out_20), .col15(main_1_out_21));
  main main_1 (
    .column(in_1), .row(in_2), .out_6(main_1_out_6), .out_7(main_1_out_7), .out_8(main_1_out_8),
    .out_9(main_1_out_9), .out_10(main_1_out_10), .out_11(main_1_out_11), .out_12(main_1_out_12),
    .out_13(main_1_out_13), .out_14(main_1_out_14), .out_15(main_1_out_15), .out_16(main_1_out_16),
    .out_17(main_1_out_17), .out_18(main_1_out_18), .out_19(main_1_out_19), .out_20(main_1_out_20),
    .out_21(main_1_out_21), .reset(button_3_out), .change_value(button_4_out));  // open: _0_if_start_pos_else_1
  Clock clock_1 (.out(clock_1_out));
  assign controlled_buffer_1_out = counter_1_q ? clock_1_out : 1'bz;  // Controlled_Buffer controlled_buffer_1
  Button button_2 (.out(button_2_out));
  Button button_3 (.out(button_3_out));
  Button button_4 (.out(button_4_out));
  reader reader_1 (
    .in_1(button_2_out), .in_2(controlled_buffer_1_out), .in_3(main_1_out_6), .in_4(main_1_out_7),
    .in_5(main_1_out_8), .in_6(main_1_out_9), .in_7(main_1_out_10), .in_8(main_1_out_11),
    .in_9(main_1_out_12), .in_10(main_1_out_13), .in_11(main_1_out_14), .in_12(main_1_out_15),
    .in_13(main_1_out_16), .in_14(main_1_out_17), .in_15(main_1_out_18), .in_16(main_1_out_19),
    .in_17(main_1_out_20), .in_18(main_1_out_21), .\адрес_говна (\reader_1_адрес_говна ),
    .\значение_говна (\reader_1_значение_говна ), .out_20(reader_1_out_20));
  RAM #(.bus("separate")) ram_1 (
    .addr(\reader_1_адрес_говна ), .din(\reader_1_значение_говна ), .data(ram_1_data), .str(reader_1_out_20),
    .clk(reader_1_out_20), .clr(button_2_out));  // open: sel, ld
  // Probe on \reader_1_адрес_говна 
endmodule

module \читатель  (
  input  \сброс ,
  input  \тактовая_залупа ,
  input  [7:0] in_3,
  input  [7:0] in_4,
  input  [15:0] \число_ебать ,
  output [7:0] \адрес_хуйни ,
  output [7:0] \знач 
);

  wire and_1_out, comparator_1_eq, comparator_1_lt, comparator_2_eq, comparator_2_gt, multiplexer_1_out,
       or_1_out, or_2_out;
  wire [3:0] buffer_1_out;
  wire [7:0] bit_extender_1_out;

  // Probe on in_3
  // Probe on in_4
  Multiplexer #(.select(4)) multiplexer_1 (
    .in0(\число_ебать [0]), .in1(\число_ебать [1]), .in2(\число_ебать [2]), .in3(\число_ебать [3]),
    .in4(\число_ебать [4]), .in5(\число_ебать [5]), .in6(\число_ебать [6]), .in7(\число_ебать [7]),
    .in8(\число_ебать [8]), .in9(\число_ебать [9]), .in10(\число_ебать [10]), .in11(\число_ебать [11]),
    .in12(\число_ебать [12]), .in13(\число_ебать [13]), .in14(\число_ебать [14]), .in15(\число_ебать [15]),
    .out(multiplexer_1_out), .sel(buffer_1_out));  // open: en
  // Probe on buffer_1_out
  Comparator #(.mode("unsigned")) comparator_1 (
    .a(in_3), .b(\адрес_хуйни ), .eq(comparator_1_eq), .lt(comparator_1_lt));  // open: gt
  Comparator #(.mode("unsigned")) comparator_2 (
    .a(in_4), .b(\адрес_хуйни ), .gt(comparator_2_gt), .eq(comparator_2_eq));  // open: lt
  assign buffer_1_out = \адрес_хуйни [3:0];  // Buffer buffer_1, 4 bits wide
  assign bit_extender_1_out = {{7{1'b0}}, multiplexer_1_out};  // Bit_Extender bit_extender_1
  or or_1 (or_1_out, comparator_1_lt, comparator_1_eq);
  or or_2 (or_2_out, comparator_2_gt, comparator_2_eq);
  Counter counter_1 (
    .D(\адрес_хуйни ), .count(1'b1), .Q(\адрес_хуйни ), .clk(\тактовая_залупа ), .clr(\сброс ));  // open: load, carry
  and and_1 (and_1_out, or_1_out, or_2_out);
  Pull_Resistor pull_resistor_1 (.node(\знач ));
  Transistor #(.\type ("n"), .width(8)) transistor_1 (.in(bit_extender_1_out), .out(\знач ), .gate(and_1_out));

  // Notes on the sheet:
  //   ot
  //   do
endmodule

module reader (
  input  in_1,
  input  in_2,
  input  [15:0] in_3,
  input  [15:0] in_4,
  input  [15:0] in_5,
  input  [15:0] in_6,
  input  [15:0] in_7,
  input  [15:0] in_8,
  input  [15:0] in_9,
  input  [15:0] in_10,
  input  [15:0] in_11,
  input  [15:0] in_12,
  input  [15:0] in_13,
  input  [15:0] in_14,
  input  [15:0] in_15,
  input  [15:0] in_16,
  input  [15:0] in_17,
  input  [15:0] in_18,
  output [7:0] \адрес_говна ,
  output out_20,
  output [7:0] \значение_говна 
);

  wire comparator_1_eq, pull_resistor_1_node;
  wire [7:0] \читатель_1_адрес_хуйни , \читатель_1_знач , \читатель_2_адрес_хуйни , \читатель_2_знач ,
       \читатель_3_адрес_хуйни , \читатель_3_знач , \читатель_4_адрес_хуйни , \читатель_4_знач ,
       \читатель_5_адрес_хуйни , \читатель_5_знач , \читатель_6_адрес_хуйни , \читатель_6_знач ,
       \читатель_7_адрес_хуйни , \читатель_7_знач , \читатель_8_адрес_хуйни , \читатель_8_знач ,
       \читатель_9_адрес_хуйни , \читатель_9_знач , \читатель_10_адрес_хуйни , \читатель_10_знач ,
       \читатель_11_адрес_хуйни , \читатель_11_знач , \читатель_12_адрес_хуйни , \читатель_12_знач ,
       \читатель_13_адрес_хуйни , \читатель_13_знач , \читатель_14_адрес_хуйни , \читатель_14_знач ,
       \читатель_15_адрес_хуйни , \читатель_15_знач , \читатель_16_адрес_хуйни , \читатель_16_знач ;

  \читатель  \u_читатель_1  (
    .\сброс (in_1), .\тактовая_залупа (pull_resistor_1_node), .\число_ебать (in_3),
    .\адрес_хуйни (\читатель_1_адрес_хуйни ), .\знач (\читатель_1_знач ), .in_4(8'hf), .in_3({8{1'b0}}));
  \читатель  \u_читатель_2  (
    .\сброс (in_1), .\тактовая_залупа (pull_resistor_1_node), .\число_ебать (in_4),
    .\адрес_хуйни (\читатель_2_адрес_хуйни ), .\знач (\читатель_2_знач ), .in_4(8'h1f), .in_3(8'h10));
  \читатель  \u_читатель_3  (
    .\сброс (in_1), .\тактовая_залупа (pull_resistor_1_node), .\число_ебать (in_5),
    .\адрес_хуйни (\читатель_3_адрес_хуйни ), .\знач (\читатель_3_знач ), .in_4(8'h2f), .in_3(8'h20));
  \читатель  \u_читатель_4  (
    .\сброс (in_1), .\тактовая_залупа (pull_resistor_1_node), .\число_ебать (in_6),
    .\адрес_хуйни (\читатель_4_адрес_хуйни ), .\знач (\читатель_4_знач ), .in_4(8'h3f), .in_3(8'h30));
  \читатель  \u_читатель_5  (
    .\сброс (in_1), .\тактовая_залупа (pull_resistor_1_node), .\число_ебать (in_7),
    .\адрес_хуйни (\читатель_5_адрес_хуйни ), .\знач (\читатель_5_знач ), .in_4(8'h4f), .in_3(8'h40));
  \читатель  \u_читатель_6  (
    .\сброс (in_1), .\тактовая_залупа (pull_resistor_1_node), .\число_ебать (in_8),
    .\адрес_хуйни (\читатель_6_адрес_хуйни ), .\знач (\читатель_6_знач ), .in_4(8'h5f), .in_3(8'h50));
  \читатель  \u_читатель_7  (
    .\сброс (in_1), .\тактовая_залупа (pull_resistor_1_node), .\число_ебать (in_9),
    .\адрес_хуйни (\читатель_7_адрес_хуйни ), .\знач (\читатель_7_знач ), .in_4(8'h6f), .in_3(8'h60));
  \читатель  \u_читатель_8  (
    .\сброс (in_1), .\тактовая_залупа (pull_resistor_1_node), .\число_ебать (in_10),
    .\адрес_хуйни (\читатель_8_адрес_хуйни ), .\знач (\читатель_8_знач ), .in_4(8'h7f), .in_3(8'h70));
  \читатель  \u_читатель_9  (
    .\сброс (in_1), .\тактовая_залупа (pull_resistor_1_node), .\число_ебать (in_11),
    .\адрес_хуйни (\читатель_9_адрес_хуйни ), .\знач (\читатель_9_знач ), .in_4(8'h8f), .in_3(8'h80));
  \читатель  \u_читатель_10  (
    .\сброс (in_1), .\тактовая_залупа (pull_resistor_1_node), .\число_ебать (in_12),
    .\адрес_хуйни (\читатель_10_адрес_хуйни ), .\знач (\читатель_10_знач ), .in_4(8'h9f), .in_3(8'h90));
  \читатель  \u_читатель_11  (
    .\сброс (in_1), .\тактовая_залупа (pull_resistor_1_node), .\число_ебать (in_13),
    .\адрес_хуйни (\читатель_11_адрес_хуйни ), .\знач (\читатель_11_знач ), .in_4(8'haf), .in_3(8'ha0));
  \читатель  \u_читатель_12  (
    .\сброс (in_1), .\тактовая_залупа (pull_resistor_1_node), .\число_ебать (in_14),
    .\адрес_хуйни (\читатель_12_адрес_хуйни ), .\знач (\читатель_12_знач ), .in_4(8'hbf), .in_3(8'hb0));
  \читатель  \u_читатель_13  (
    .\сброс (in_1), .\тактовая_залупа (pull_resistor_1_node), .\число_ебать (in_15),
    .\адрес_хуйни (\читатель_13_адрес_хуйни ), .\знач (\читатель_13_знач ), .in_4(8'hcf), .in_3(8'hc0));
  \читатель  \u_читатель_14  (
    .\сброс (in_1), .\тактовая_залупа (pull_resistor_1_node), .\число_ебать (in_16),
    .\адрес_хуйни (\читатель_14_адрес_хуйни ), .\знач (\читатель_14_знач ), .in_4(8'hdf), .in_3(8'hd0));
  \читатель  \u_читатель_15  (
    .\сброс (in_1), .\тактовая_залупа (pull_resistor_1_node), .\число_ебать (in_17),
    .\адрес_хуйни (\читатель_15_адрес_хуйни ), .\знач (\читатель_15_знач ), .in_4(8'hef), .in_3(8'he0));
  \читатель  \u_читатель_16  (
    .\сброс (in_1), .\тактовая_залупа (pull_resistor_1_node), .\число_ебать (in_18),
    .\адрес_хуйни (\читатель_16_адрес_хуйни ), .\знач (\читатель_16_знач ), .in_4({8{1'b1}}), .in_3(8'hf0));
  xor xor_1 (out_20, comparator_1_eq, pull_resistor_1_node);
  Comparator #(.mode("unsigned")) comparator_1 (
    .a({8{1'b1}}), .b(\адрес_говна ), .eq(comparator_1_eq));  // open: gt, lt
  Pull_Resistor pull_resistor_1 (.node(pull_resistor_1_node));
  Transistor transistor_1 (.in(in_2), .out(pull_resistor_1_node), .gate(comparator_1_eq));
  assign \адрес_говна  = \читатель_1_адрес_хуйни  | \читатель_2_адрес_хуйни  | \читатель_3_адрес_хуйни  | \читатель_4_адрес_хуйни  | \читатель_5_адрес_хуйни  | \читатель_6_адрес_хуйни  | \читатель_7_адрес_хуйни  | \читатель_8_адрес_хуйни  | \читатель_9_адрес_хуйни  | \читатель_10_адрес_хуйни  | \читатель_11_адрес_хуйни  | \читатель_12_адрес_хуйни  | \читатель_13_адрес_хуйни  | \читатель_14_адрес_хуйни  | \читатель_15_адрес_хуйни  | \читатель_16_адрес_хуйни ;  // OR_Gate or_1, 8 bits wide
  // Probe on \значение_говна 
  // Probe on \адрес_говна 
  assign \значение_говна  = \читатель_1_знач  | \читатель_2_знач  | \читатель_3_знач  | \читатель_4_знач  | \читатель_5_знач  | \читатель_6_знач  | \читатель_7_знач  | \читатель_8_знач  | \читатель_9_знач  | \читатель_10_знач  | \читатель_11_знач  | \читатель_12_знач  | \читатель_13_знач  | \читатель_14_знач  | \читатель_15_знач  | \читатель_16_знач ;  // OR_Gate or_2, 8 bits wide

  // Notes on the sheet:
  //   значение строк ебаного дисплея\
  //   щелбан чтоб обнулить
  //   щелчок бля для записи
endmodule

module \интел_228  (
  input  [7:0] in_1
);

  wire cdm_8_mark5_1_p2, cdm_8_mark5_1_p3, cdm_8_mark5_1_p5, cdm_8_mark5_1_p6, cdm_8_mark5_1_p8,
       cdm_8_mark5_1_p9, cdm_8_mark5_1_p10, clock_1_out, comparator_1_eq, decoder_1_out0, decoder_1_out1,
       decoder_2_out0, decoder_2_out1, not_1_out, not_2_out, not_3_out;
  wire [7:0] cdm_8_mark5_1_p4, cdm_8_mark5_1_p11, cdm_8_mark5_1_p12, cdm_8_mark5_1_p13,
       controlled_buffer_3_out;

  Comparator #(.mode("unsigned")) comparator_1 (.a(cdm_8_mark5_1_p4), .b(8'he4), .eq(comparator_1_eq));  // open: gt, lt
  not not_1 (not_1_out, comparator_1_eq);
  Clock clock_1 (.out(clock_1_out));
  // Probe on cdm_8_mark5_1_p4
  // Probe on cdm_8_mark5_1_p3
  // Probe on cdm_8_mark5_1_p2
  Controlled_Buffer controlled_buffer_1 (.in(clock_1_out), .en(not_1_out));  // open: out
  // Probe on cdm_8_mark5_1_p5
  // CdM_8_mark5 cdm_8_mark5_1: pin names not known; wires that end beside it: not_1_out, cdm_8_mark5_1_p2, cdm_8_mark5_1_p3, cdm_8_mark5_1_p4, cdm_8_mark5_1_p5, cdm_8_mark5_1_p6, cdm_8_mark5_1_p6, cdm_8_mark5_1_p8, cdm_8_mark5_1_p9, cdm_8_mark5_1_p10, cdm_8_mark5_1_p11, cdm_8_mark5_1_p12, cdm_8_mark5_1_p13, in_1
  not not_2 (not_2_out, cdm_8_mark5_1_p10);
  assign cdm_8_mark5_1_p13 = cdm_8_mark5_1_p10 ? controlled_buffer_3_out : 8'bz;  // Controlled_Buffer controlled_buffer_2
  Decoder #(.disabled(0)) decoder_1 (
    .out0(decoder_1_out0), .out1(decoder_1_out1), .sel(cdm_8_mark5_1_p8), .en(cdm_8_mark5_1_p9));
  assign controlled_buffer_3_out = not_2_out ? cdm_8_mark5_1_p12 : 8'bz;  // Controlled_Buffer controlled_buffer_3
  // Probe on cdm_8_mark5_1_p11
  Decoder #(.disabled(0)) decoder_2 (
    .out0(decoder_2_out0), .out1(decoder_2_out1), .sel(cdm_8_mark5_1_p10), .en(decoder_1_out1));
  not not_3 (not_3_out, cdm_8_mark5_1_p10);
  Pull_Resistor pull_resistor_1 (.node(decoder_1_out0));
  ROM rom_1 (.addr(cdm_8_mark5_1_p11), .data(controlled_buffer_3_out), .sel(decoder_1_out0));
  RAM #(.bus("separate")) ram_1 (
    .addr(cdm_8_mark5_1_p11), .din(controlled_buffer_3_out), .data(controlled_buffer_3_out),
    .sel(decoder_2_out1), .ld(cdm_8_mark5_1_p10));  // open: str, clk, clr
  RAM #(.bus("separate")) ram_2 (
    .addr(cdm_8_mark5_1_p11), .din(controlled_buffer_3_out), .data(controlled_buffer_3_out), .str(not_3_out),
    .sel(decoder_2_out0), .clk(clock_1_out));  // open: ld, clr

  // Notes on the sheet:
  //   code
  //   поле сейчас (отседа четаем)
  //   поле на след шаге сюда пишем
  //   contents of rom_1 (hex, n*v repeats v):
  //   d2 f0 19 b4 13 d2 1 19 b4 13 d2 e 19 b4 13 d2 10 19 b4 13 d2 10 19 b4 13 d2 f1 19 b4 13 d2 1 19 b4
  //   13 d2 f0 19 b4 13 89 d2 3 7e e1 33 d2 1 a6 ee 44 b4 0 e0 41 d2 2 7b e1 3f d2 1 a6 ee 44 d2 0 a6 d2
  //   10 19 5 e1 0 d1 f d2 f0 19 b4 13 d2 f1 19 b4 13 d2 e 19 b4 13 d2 10 19 b4 13 d2 10 19 b4 13 d2 1 19
  //   b4 13 d2 f1 19 b4 13 d2 f0 19 b4 13 d2 f 19 d2 3 7e e1 81 d2 1 a6 ee 92 b4 0 e0 8f d2 2 7b e1 8d d2
  //   1 a6 ee 92 d2 0 a6 d2 10 19 d2 f 76 e1 4c d1 0 d2 f0 19 b4 13 d2 1 19 b4 13 d2 10 19 b4 13 19 b4 13
  //   89 b4 13 89 b4 13 d2 f0 19 b4 13 19 b4 13 d2 11 19 d2 3 7e e1 c9 d2 1 a6 ee da b4 0 e0 d7 d2 2 7b e1
  //   d5 d2 1 a6 ee da d2 0 a6 8d 5 e1 9c d2 e4 a e1 0 d4
endmodule
